# Fritzing sketch Sentinel_v1 (saved by Fritzing 0.9.3b)
circuit board: 3.55743cm x 3.18158cm
breadboards: 1

parts:
  RST = female pin header, 10 pins [form="♀ (female)"]
  U1 = Voltage Regulator - 5V [package="DPak [SMD]"]
  Vin = female pin header, 2 pins [form="♀ (female)"]
  PIR = female pin header, 3 pins [form="♀ (female)"]
  5V = female pin header, 2 pins [form="♀ (female)"]
  30V = female pin header, 2 pins [form="♀ (female)"]
  BJT = TRANSISTOR_NPN_2 [package=to-92]
  R3 = Resistor [tolerance=±5% resistance=220 package=THT]
  Buzzer = Piezo Speaker
  5K = Resistor [tolerance=±5% resistance=220 package=THT]

nets:
  N1: RST.pin6, BJT.B
  N2: RST.pin7, PIR.pin2, 5K.Pin_1
  N3: RST.pin9, U1.output_voltage, PIR.pin1, 5V.pin1
  N4: RST.pin10, U1.GND, Vin.pin2, PIR.pin3, 5V.pin2, 30V.pin2, BJT.E, Buzzer.pin2, 5K.Pin_0
  N5: U1.input_voltage, Vin.pin1
  N6: 30V.pin1, R3.Pin_0
  N7: BJT.C, R3.Pin_1, Buzzer.pin1

notes:
  Gnd
  Vbatt
  V+
  13
  12
  14
  16
  E
  5V
